// Logisim project microp.circ as structural Verilog: 7 circuits, main circuit RegisterFile
// Register File
module RegisterFile (
  input  [2:0] rd,
  input  [15:0] Datain,
  input  Register_Load,
  input  clock,
  output [15:0] Data_Out1,
  output [15:0] Data_Out2,
  output [15:0] Data_Out3,
  output [15:0] Data_Out4,
  output [15:0] Data_Out5,
  output [15:0] Data_Out6,
  output [15:0] Data_Out7,
  output [15:0] Data_Out8
);

  wire and_1_out, and_2_out, and_3_out, and_4_out, and_5_out, and_6_out, and_7_out, and_8_out,
       decoder_1_out0, decoder_1_out1, decoder_1_out2, decoder_1_out3, decoder_1_out4, decoder_1_out5,
       decoder_1_out6, decoder_1_out7;

  Decoder #(.select(3), .enable("false")) decoder_1 (
    .out0(decoder_1_out0), .out1(decoder_1_out1), .out2(decoder_1_out2), .out3(decoder_1_out3),
    .out4(decoder_1_out4), .out5(decoder_1_out5), .out6(decoder_1_out6), .out7(decoder_1_out7), .sel(rd));
  and and_1 (and_1_out, decoder_1_out0, Register_Load);
  and and_2 (and_2_out, decoder_1_out1, Register_Load);
  and and_3 (and_3_out, decoder_1_out2, Register_Load);
  and and_4 (and_4_out, decoder_1_out3, Register_Load);
  and and_5 (and_5_out, decoder_1_out4, Register_Load);
  and and_6 (and_6_out, decoder_1_out5, Register_Load);
  and and_7 (and_7_out, decoder_1_out6, Register_Load);
  and and_8 (and_8_out, decoder_1_out7, Register_Load);
  Register #(.width(16)) register_1 (.D(Datain), .en(and_1_out), .Q(Data_Out1), .clk(clock));  // open: clr
  Register #(.width(16)) register_2 (.D(Datain), .en(and_2_out), .Q(Data_Out2), .clk(clock));  // open: clr
  Register #(.width(16)) register_3 (.D(Datain), .en(and_3_out), .Q(Data_Out3), .clk(clock));  // open: clr
  Register #(.width(16)) register_4 (.D(Datain), .en(and_4_out), .Q(Data_Out4), .clk(clock));  // open: clr
  Register #(.width(16)) register_5 (.D(Datain), .en(and_5_out), .Q(Data_Out5), .clk(clock));  // open: clr
  Register #(.width(16)) register_6 (.D(Datain), .en(and_6_out), .Q(Data_Out6), .clk(clock));  // open: clr
  Register #(.width(16)) register_7 (.D(Datain), .en(and_7_out), .Q(Data_Out7), .clk(clock));  // open: clr
  Register #(.width(16)) register_8 (.D(Datain), .en(and_8_out), .Q(Data_Out8), .clk(clock));  // open: clr

  // Notes on the sheet:
  //   Register_Load: pull=down
endmodule

module ALU (
  input  [15:0] Source1,
  input  [15:0] Source2,
  input  [5:0] ALUControl,
  output [15:0] Output
);

  wire [15:0] adder_1_out, adder_2_out, and_1_out, multiplexer_1_out, not_1_out, or_1_out, subtractor_1_out,
       subtractor_2_out, xor_1_out;

  Adder #(.width(16)) adder_1 (.a(Source1), .b(16'h1), .out(adder_1_out));  // open: cin, cout
  Subtractor #(.width(16)) subtractor_1 (.a(Source1), .b(16'h1), .out(subtractor_1_out));  // open: bin, bout
  assign not_1_out = ~Source1;  // NOT_Gate not_1, 16 bits wide
  Adder #(.width(16)) adder_2 (.a(Source1), .b(Source2), .out(adder_2_out));  // open: cin, cout
  Subtractor #(.width(16)) subtractor_2 (.a(Source1), .b(Source2), .out(subtractor_2_out));  // open: bin, bout
  assign and_1_out = Source1 & Source2;  // AND_Gate and_1, 16 bits wide
  assign or_1_out = Source1 | Source2;  // OR_Gate or_1, 16 bits wide
  assign xor_1_out = Source1 ^ Source2;  // XOR_Gate xor_1, 16 bits wide
  Multiplexer #(.select(3), .width(16), .enable("false")) multiplexer_1 (
    .in0(Source1), .in1(not_1_out), .in2(adder_1_out), .in3(subtractor_1_out), .out(multiplexer_1_out),
    .sel(ALUControl[2:0]));  // open: in4, in5, in6, in7
  Multiplexer #(.select(3), .width(16), .enable("false")) multiplexer_2 (
    .in0(adder_2_out), .in1(subtractor_2_out), .in2(and_1_out), .in3(or_1_out), .in4(xor_1_out),
    .in7(multiplexer_1_out), .out(Output), .sel(ALUControl[5:3]));  // open: in5, in6
endmodule

// PC
module PogramCOUNTER (
  input  [11:0] jumpin,
  input  Clk,
  input  isChangeCounter,
  input  fetch1,
  input  [11:0] _1,
  output [11:0] \output 
);

  wire adder_1_cout, adder_2_cout, not_1_out, or_1_out;
  wire [11:0] adder_1_out, adder_2_out, multiplexer_1_out;

  Adder #(.width(12)) adder_1 (.a(jumpin), .b(\output ), .out(adder_1_out), .cout(adder_1_cout));  // open: cin
  Multiplexer #(.width(12)) multiplexer_1 (
    .in0(adder_1_out), .in1(adder_2_out), .out(multiplexer_1_out), .sel(isChangeCounter), .en(fetch1));
  or or_1 (or_1_out, adder_2_cout, adder_1_cout);
  Register #(.width(12)) register_1 (.D(multiplexer_1_out), .Q(\output ), .clk(not_1_out), .clr(or_1_out));  // open: en
  Adder #(.width(12)) adder_2 (.a(\output ), .b(_1), .out(adder_2_out), .cout(adder_2_cout));  // open: cin
  not not_1 (not_1_out, Clk);
endmodule

// CPU
module yeni (
  input  [15:0] Din,
  output [11:0] ADDR,
  output [15:0] DOut
);

  wire clock_1_out, undriven, undriven_2, undriven_3, undriven_4;
  wire [2:0] instructionsplitter_1_dest, instructionsplitter_1_src1, instructionsplitter_1_src2;
  wire [5:0] instructionsplitter_1_alucode;
  wire [11:0] adder_1_out, instructionsplitter_1_relative_offset, multiplexer_4_out, pogramcounter_1_output;
  wire [15:0] alu_1_output, multiplexer_2_out, registerfile_1_data_out1, registerfile_1_data_out2,
       registerfile_1_data_out3, registerfile_1_data_out4, registerfile_1_data_out5,
       registerfile_1_data_out6, registerfile_1_data_out7, registerfile_1_data_out8;
  wire [15:12] multiplexer_4_out_2;

  Clock clock_1 (.out(clock_1_out));
  PogramCOUNTER pogramcounter_1 (
    .jumpin(adder_1_out), ._1(12'h1), .\output (pogramcounter_1_output), .Clk(clock_1_out));  // open: isChangeCounter, fetch1
  Multiplexer #(.width(12), .enable("false")) multiplexer_1 (
    .in0(pogramcounter_1_output), .in1(multiplexer_4_out), .out(ADDR), .sel(undriven_4));
  Adder #(.width(12)) adder_1 (
    .a(instructionsplitter_1_relative_offset), .b(pogramcounter_1_output), .out(adder_1_out));  // open: cin, cout
  RegisterFile registerfile_1 (
    .rd(instructionsplitter_1_dest), .Datain(multiplexer_2_out), .Register_Load(undriven),
    .clock(clock_1_out), .Data_Out1(registerfile_1_data_out1), .Data_Out2(registerfile_1_data_out2),
    .Data_Out3(registerfile_1_data_out3), .Data_Out4(registerfile_1_data_out4),
    .Data_Out5(registerfile_1_data_out5), .Data_Out6(registerfile_1_data_out6),
    .Data_Out7(registerfile_1_data_out7), .Data_Out8(registerfile_1_data_out8));
  Multiplexer #(.width(16), .enable("false")) multiplexer_2 (
    .in0(alu_1_output), .in1(Din), .out(multiplexer_2_out), .sel(undriven_3));
  Multiplexer #(.select(3), .width(16), .enable("false")) multiplexer_3 (
    .in0(registerfile_1_data_out8), .in1(registerfile_1_data_out7), .in2(registerfile_1_data_out6),
    .in3(registerfile_1_data_out5), .in4(registerfile_1_data_out4), .in5(registerfile_1_data_out3),
    .in6(registerfile_1_data_out2), .in7(registerfile_1_data_out1), .out(DOut),
    .sel(instructionsplitter_1_src1));
  ALU alu_1 (
    .Source1(DOut), .Source2({multiplexer_4_out_2, multiplexer_4_out}),
    .ALUControl(instructionsplitter_1_alucode), .Output(alu_1_output));
  InstructionSplitter instructionsplitter_1 (
    .Instruction(Din[11:0]), .IRLoad(undriven_2), .clk(clock_1_out), .ALUCode(instructionsplitter_1_alucode),
    .src1(instructionsplitter_1_src1), .src2(instructionsplitter_1_src2), .dest(instructionsplitter_1_dest),
    .relative_Offset(instructionsplitter_1_relative_offset));
  Multiplexer #(.select(3), .width(16), .enable("false")) multiplexer_4 (
    .in0(registerfile_1_data_out8), .in1(registerfile_1_data_out7), .in2(registerfile_1_data_out6),
    .in3(registerfile_1_data_out5), .in4(registerfile_1_data_out4), .in5(registerfile_1_data_out3),
    .in6(registerfile_1_data_out2), .in7(registerfile_1_data_out1),
    .out({multiplexer_4_out_2, multiplexer_4_out}), .sel(instructionsplitter_1_src2));

  // Notes on the sheet:
  //   Go to Control Unit
  //   Mux
  //   RegisterLoad
  //   IRLoad
  //   Armux
endmodule

module ControlUnit (
  input  [2:0] in_1,
  input  [2:0] in_2
);

  wire [2:0] undriven;

  Multiplexer #(.select(2), .width(3), .enable("false")) multiplexer_1 (
    .in1(undriven), .in2(in_2), .in3(in_1));  // open: in0, out, sel
endmodule

module main (
);

  wire [11:0] yeni_1_p2;
  wire [15:0] ram_1_data, yeni_1_p3;

  RAM #(.addrWidth(12), .dataWidth(16), .bus("separate")) ram_1 (
    .addr(yeni_1_p2), .din(yeni_1_p3), .data(ram_1_data));  // open: str, sel, clk, ld, clr
  // yeni yeni_1: pin names not known; wires that end beside it: ram_1_data, yeni_1_p2, yeni_1_p3
endmodule

module InstructionSplitter (
  input  [11:0] Instruction,
  input  IRLoad,
  input  clk,
  output [5:0] ALUCode,
  output [2:0] src1,
  output [2:0] src2,
  output [2:0] dest,
  output [11:0] relative_Offset
);

  Register #(.width(12)) register_1 (
    .D(Instruction), .en(IRLoad), .Q({ALUCode, relative_Offset[5:3], dest}), .clk(clk));  // open: clr

  assign {relative_Offset[11:6], relative_Offset[2:0]} = {ALUCode, dest};
  assign src1 = ALUCode[2:0];
  assign src2 = relative_Offset[5:3];
endmodule
